# Fritzing sketch SoccerTable V3 (saved by Fritzing 0.9.3b)
circuit board: 3.58554cm x 5.14956cm
circuit board: 5.14956cm x 3.58554cm
circuit board: 5.14956cm x 3.58554cm
breadboards: 1

parts:
  S1_Goal_1 = Pushbutton [package="[THT]"]
  S2_Goal_2 = Pushbutton [package="[THT]"]
  S3_Start/Stop = Pushbutton [package="[THT]"]
  S4_Settings = Pushbutton [package="[THT]"]
  WeMos_D1 = WeMos D1 Mini
  H2_1_OLED = female pin header, 6 pins [form="♀ (female)"]
  H1_1_Buttons = female pin header, 6 pins [form="♀ (female)"]
  1000yF1 = Capacitor Polarized [package=panasonic_g]
  I2C_OLED_Display = OLED 0.96" 128x64 I2C SSD1306
  H3_2_Shift_IN = female pin header, 10 pins [form="♀ (female)"]
  H3_1_Shift_I2C = female pin header, 4 pins [form="♀ (female)"]
  H2_2_OLED2 = female pin header, 6 pins [form="♀ (female)"]
  H1_2_Buttons = female pin header, 6 pins [form="♀ (female)"]
  VCC_IN = Screw terminal - 2 pins [package=THT]
  J2_Neopixels = shrouded pin header, 6 pins [form="♂ (shrouded male)"]
  J1_1_Sensors_1 = shrouded pin header, 8 pins [form="♂ (shrouded male)"]
  J1_2_Sensors_2 = shrouded pin header, 8 pins [form="♂ (shrouded male)"]
  Speaker_Jack = Audio Jack (TRS) 3.5mm [package="4Ucon 08780 [THT]"]
  DFRobot_DFPlayer_Mini1 = DFRobot DFPlayer Mini [part_number=DFR0299]
  H3_1_MP3_Shield = female pin header, 8 pins [form="♀ (female)"]
  H3_2_MP3_Shield = female pin header, 8 pins [form="♀ (female)"]

nets:
  N1: S1_Goal_1.Pin_2, H1_1_Buttons.pin5
  N2: S1_Goal_1.Pin_3, S1_Goal_1.Pin_4, S2_Goal_2.Pin_1, S2_Goal_2.Pin_2, S3_Start/Stop.Pin_3, S3_Start/Stop.Pin_4, S4_Settings.Pin_1, S4_Settings.Pin_2, H2_1_OLED.pin5, I2C_OLED_Display.VCC
  N3: S2_Goal_2.Pin_3, S2_Goal_2.Pin_4, H1_1_Buttons.pin2
  N4: S3_Start/Stop.Pin_1, S3_Start/Stop.Pin_2, H1_1_Buttons.pin4
  N5: S4_Settings.Pin_3, H1_1_Buttons.pin3
  N6: WeMos_D1.3V3, H3_1_Shift_I2C.pin1, H2_2_OLED2.pin4, J1_1_Sensors_1.pin7, J1_2_Sensors_2.pin7
  N7: WeMos_D1.5V, 1000yF1.-, VCC_IN.pin2, J2_Neopixels.pin6
  N8: WeMos_D1.D1, H3_1_Shift_I2C.pin3, H2_2_OLED2.pin2
  N9: WeMos_D1.D2, H3_1_Shift_I2C.pin4, H2_2_OLED2.pin3
  N10: WeMos_D1.D3, J2_Neopixels.pin5
  N11: WeMos_D1.D4, H3_2_Shift_IN.pin1
  N12: WeMos_D1.G, 1000yF1.+, H3_1_Shift_I2C.pin2, H2_2_OLED2.pin5, VCC_IN.pin1, J2_Neopixels.pin4, J1_1_Sensors_1.pin8, J1_2_Sensors_2.pin8
  N13: H2_1_OLED.pin2, I2C_OLED_Display.SCA
  N14: H2_1_OLED.pin3, I2C_OLED_Display.SCL
  N15: H2_1_OLED.pin4, I2C_OLED_Display.GND
  N16: H3_2_Shift_IN.pin2, J1_2_Sensors_2.pin5
  N17: H3_2_Shift_IN.pin3, J1_2_Sensors_2.pin6
  N18: H3_2_Shift_IN.pin4, J1_1_Sensors_1.pin5
  N19: H3_2_Shift_IN.pin5, J1_1_Sensors_1.pin6
  N20: H3_2_Shift_IN.pin6, H1_2_Buttons.pin2
  N21: H3_2_Shift_IN.pin7, H1_2_Buttons.pin3
  N22: H3_2_Shift_IN.pin8, H1_2_Buttons.pin4
  N23: H3_2_Shift_IN.pin9, H1_2_Buttons.pin5
  N24: Speaker_Jack.Sleeve, DFRobot_DFPlayer_Mini1.GND-1, DFRobot_DFPlayer_Mini1.GND-2, H3_1_MP3_Shield.pin7
  N25: Speaker_Jack.Ring, DFRobot_DFPlayer_Mini1.DAC_R
  N26: Speaker_Jack.Tip, DFRobot_DFPlayer_Mini1.DAC_L
  N27: DFRobot_DFPlayer_Mini1.VCC, H3_1_MP3_Shield.pin8
  N28: DFRobot_DFPlayer_Mini1.RX, H3_2_MP3_Shield.pin5
  N29: DFRobot_DFPlayer_Mini1.TX, H3_2_MP3_Shield.pin4
  N30: DFRobot_DFPlayer_Mini1.BUSY, H3_2_MP3_Shield.pin6

custom parts:
  WeMos D1 Mini: The D1 mini is a mini wifi board based on ESP-8266EX.
